# Fritzing sketch WakeupLight (saved by Fritzing 0.9.0b)
breadboards: 1

parts:
  RTC1 = DS1307 RTC Breakout
  7SEG1 = 7-Segment LED I2C Backpack (yellow)
  S3 = Momentary Switch [package=ksa_sealed_tac_switch]
  S4 = Momentary Switch [package=ksa_sealed_tac_switch]
  Part1 = Arduino Pro Mini v13
  JACK1 = 2.1mm Barrel Jack with Terminal Block
  Q1 = MOSFET-NCHANNEL [part_number=STP16NF06L package=to220v]

nets:
  GND: RTC1.GND, 7SEG1.GND, S3.4, Part1.GND, JACK1.NEG, Q1.S
  5V: RTC1.5V, 7SEG1.V+, Part1.VCC
  N1: RTC1.SDA, Part1.A4
  N2: RTC1.SCL, 7SEG1.SCL, Part1.A5
  N3: S3.2, Part1.D3_PWM
  N4: S3.3, S4.1
  N5: S4.4, Part1.D2
  N6: Part1.RAW, JACK1.POS
  N7: Part1.D6_PWM, Q1.G

notes:
  12V @ 2A
  To Strip
  12V   GND

custom parts:
  DS1307 RTC Breakout: DS1307 Real-time Clock Breakout Board with Battery
  7-Segment LED I2C Backpack (yellow): 4-digit, 7-segment LED Display with I2C Control
